# Fritzing sketch gaspart (saved by Fritzing 0.9.3b)
breadboards: 1

parts:
  U2 = NodeMCU V1.0
  M2 = STM32407VG Discovery
  Parça1 = MQ-4
  Parça2 = Arduino Uno (Rev3) - ICSP
  Parça3 = IFR520 MOS module [package=THT]
  VCC1 = Battery block 9V  # not connected
  F1 = Fan - Ventilador [package=THT]
  J1 = Piezo Speaker

nets:
  N1: U2.GND, M2.GND-49, M2.GND-99, M2.GND-105, Parça1.DO, J1.pin1
  N2: U2.RX, M2.PA2
  N3: U2.TX, M2.PA3
  N4: M2.PE15, Parça2.D11_PWM/MOSI
  N5: M2.PE13, Parça2.D9_PWM
  N6: M2.PE14, Parça2.D10_PWM/SS
  N7: M2.PE12, Parça2.D8
  N8: M2.PC4, Parça1.AO
  N9: M2.5V-98, Parça1.GND
  N10: Parça2.GND, Parça3.pin3
  N11: Parça2.D3_PWM, Parça3.pin1
  N12: Parça3.pin4, F1.5V
  N13: Parça3.pin5, F1.GND

notes:
  esp8266 weden data çekmek için kullanıldı
  arduino IRF520 için kullanıldı

custom parts:
  NodeMCU V1.0: ESP8266 based NodeMCU
  STM32407VG Discovery: The STM32F4DISCOVERY Discovery kit allows users to easily develop applications with the STM32F407VG high performance microcontroller with the ARM® Cortex®-M4 32-bit core. It includes everything required either for beginners or for experienced users to get quickly started.Based on STM32F407VG, it includes an ST-LINK/V2 or ST-LINK/V2-A embedded debug tool, two ST-MEMS digital accelerometers, a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
  Fan - Ventilador: Ventilador de 2 pines, se encuentra comunmente en computadoras de escritorio
