# Fritzing sketch mesafepart (saved by Fritzing 0.9.3b)
breadboards: 1

parts:
  J5 = Basic Servo
  M4 = STM32407VG Discovery
  U4 = NodeMCU V1.0
  hc-sr1 = hc-sr04

nets:
  GND: J5.gnd, M4.GND-49, M4.GND-74, M4.GND-99, U4.GND, hc-sr1.GND
  VCC: J5.vcc, M4.5V-73, M4.5V-98, hc-sr1.VCC
  N1: M4.PE9, hc-sr1.Echo
  N2: M4.PA3, U4.TX
  N3: M4.PE8, hc-sr1.Trig
  N4: M4.PA2, U4.RX

notes:
  esp8266 weden data çekmek için kullanıldı

custom parts:
  STM32407VG Discovery: The STM32F4DISCOVERY Discovery kit allows users to easily develop applications with the STM32F407VG high performance microcontroller with the ARM® Cortex®-M4 32-bit core. It includes everything required either for beginners or for experienced users to get quickly started.Based on STM32F407VG, it includes an ST-LINK/V2 or ST-LINK/V2-A embedded debug tool, two ST-MEMS digital accelerometers, a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
  NodeMCU V1.0: ESP8266 based NodeMCU
