# Fritzing sketch rainpart (saved by Fritzing 0.9.3b)
breadboards: 1

parts:
  MH-ET_LIVE_ESP32_DEVKIT1 = MH-ET LIVE ESP32 DEVKIT 38 pins
  SM1 = 28BYJ-48 Stepper Motor [part_number=28BYJ-48]
  Driver1 = 28BYJ-48 Driver Module [part_number=ULN2003 package=THT]
  M1 = STM32407VG Discovery
  YL-83_-_Detection_Board1 = YL-83 Rain Sensor - Detection Board
  YL-83_-_Control_Board1 = YL-83 Rain Sensor - Control Board
  U1 = NodeMCU V1.0

nets:
  N1: MH-ET_LIVE_ESP32_DEVKIT1.TXD0, M1.PD9
  N2: MH-ET_LIVE_ESP32_DEVKIT1.RXD0, M1.PD8
  GND: MH-ET_LIVE_ESP32_DEVKIT1.GND, Driver1.GND, M1.GND-24, M1.GND-49, M1.GND-99, YL-83_-_Control_Board1.GND, U1.GND
  N3: MH-ET_LIVE_ESP32_DEVKIT1.IO19, Driver1.IN1
  N4: MH-ET_LIVE_ESP32_DEVKIT1.IO18, Driver1.IN2
  N5: MH-ET_LIVE_ESP32_DEVKIT1.IO5, Driver1.IN3
  N6: MH-ET_LIVE_ESP32_DEVKIT1.IO17, Driver1.IN4
  N7: SM1.pink-pin, Driver1.blue-pin
  N8: SM1.yellow-pin, Driver1.pink-pin
  N9: SM1.orange-pin, Driver1.yellow-pin
  N10: SM1.red-pin, Driver1.orange-pin
  N11: Driver1.Vmotor, M1.5V-73, M1.5V-98, YL-83_-_Control_Board1.VCC
  N12: M1.PA3, U1.TX
  N13: M1.PA1, YL-83_-_Control_Board1.DO
  N14: M1.PA2, U1.RX
  N15: YL-83_-_Detection_Board1.POS, YL-83_-_Control_Board1.POS
  N16: YL-83_-_Detection_Board1.NEG, YL-83_-_Control_Board1.NEG

notes:
  devkit step motor sürmek için kullanıldı
  esp8266 weden data çekmek için kullanıldı

custom parts:
  MH-ET LIVE ESP32 DEVKIT 38 pins: http://mh.nodebb.com/topic/2/mh-et-live-esp32-devkit
  28BYJ-48 Stepper Motor: Unipolar Stepper Motor 28BYJ-48 Top coil - pink & orange Bottom coil - blue & yellow Common rail - red Connector pins: blue - pink - yellow - orange - red
  28BYJ-48 Driver Module: Generic male header
  STM32407VG Discovery: The STM32F4DISCOVERY Discovery kit allows users to easily develop applications with the STM32F407VG high performance microcontroller with the ARM® Cortex®-M4 32-bit core. It includes everything required either for beginners or for experienced users to get quickly started.Based on STM32F407VG, it includes an ST-LINK/V2 or ST-LINK/V2-A embedded debug tool, two ST-MEMS digital accelerometers, a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
  YL-83 Rain Sensor - Detection Board: The YL-83 is a rain sensor that has more resistance when dry and less resistance when wet. The module runs at 5V.
  YL-83 Rain Sensor - Control Board: The YL-83 is a rain sensor that has more resistance when dry and less resistance when wet. The module runs at 5V.
  NodeMCU V1.0: ESP8266 based NodeMCU
