# Fritzing sketch touchpart (saved by Fritzing 0.9.3b)
breadboards: 1

parts:
  U3 = NodeMCU V1.0
  M3 = STM32407VG Discovery
  J2 = Piezo Speaker
  J3 = Basic Servo
  TTP223B1 = TTP223B Capacitive Touch Sensor Module

nets:
  GND: U3.GND, M3.GND-49, M3.GND-99, M3.GND-105, J2.pin1, J3.gnd, TTP223B1.GND
  N1: U3.RX, M3.PA2
  N2: U3.TX, M3.PA3
  N3: M3.PC5, TTP223B1.SIG
  VCC: M3.5V-73, M3.5V-98, J3.vcc, TTP223B1.VCC

notes:
  esp8266 weden data çekmek için kullanıldı

custom parts:
  NodeMCU V1.0: ESP8266 based NodeMCU
  STM32407VG Discovery: The STM32F4DISCOVERY Discovery kit allows users to easily develop applications with the STM32F407VG high performance microcontroller with the ARM® Cortex®-M4 32-bit core. It includes everything required either for beginners or for experienced users to get quickly started.Based on STM32F407VG, it includes an ST-LINK/V2 or ST-LINK/V2-A embedded debug tool, two ST-MEMS digital accelerometers, a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
  TTP223B Capacitive Touch Sensor Module: The TTP223B capacitive touch sensor module uses the TTP223B IC. The appropriate voltage is approximately 2 to 5.5 volts.
